# Fritzing sketch fajker (saved by Fritzing 0.9.3b)
breadboards: 3

parts:
  Bauteil1 = Arduino Nano (Rev3.0)
  U2 = LCD-16X2 [package=lcd-16x2_noholes]
  LED1 = LED - 3mm [color="Red (633nm)" package="3 mm [THT]"]
  LED2 = LED - 3mm [color="Red (633nm)" package="3 mm [THT]"]
  Bauteil2 = Thumb Joystick
  J1 = Piezo Speaker
  R1 = Resistor [tolerance=±5% resistance=220 package="2512 [SMD]"]
  R2 = Resistor [tolerance=±5% resistance=220 package="2512 [SMD]"]
  R3 = Resistor [tolerance=±5% resistance=220 package="2512 [SMD]"]
  R4 = Rotary Potentiometer (Small) [maximum_resistance=100kΩ package=THT]
  Bauteil3 = RFID-RC522-v2

nets:
  N1: Bauteil1.D2, U2.RS
  N2: Bauteil1.D3, U2.E
  N3: Bauteil1.D4, U2.DB4
  N4: Bauteil1.D5, U2.DB5
  N5: Bauteil1.D6, U2.DB6
  N6: Bauteil1.D7, U2.DB7
  N7: Bauteil1.D8, Bauteil2.SEL
  N8: Bauteil1.D9, Bauteil3.RST
  N9: Bauteil1.D10, Bauteil3.MOSI
  N10: Bauteil1.D11/MOSI, Bauteil3.SDA
  N11: Bauteil1.D12/MISO, Bauteil3.MISO
  GND: Bauteil1.GND, U2.VSS, U2.R_W, U2.K, LED1.anode, LED2.anode, Bauteil2.GND, J1.pin1, R4.leg1, Bauteil3.GND
  5V: Bauteil1.5V, U2.VDD, Bauteil2.VCC, R2.Pin_1, R4.leg2
  N12: Bauteil1.A5, R1.Pin_0
  N13: Bauteil1.A4, R3.Pin_0
  N14: Bauteil1.A3, J1.pin2
  N15: Bauteil1.A2, Bauteil2.HORZ
  N16: Bauteil1.A1, Bauteil2.VERT
  3V3: Bauteil1.3V3, Bauteil3.3.3V
  N17: Bauteil1.D13/SCK, Bauteil3.SCK
  N18: U2.VO, R4.wiper
  N19: U2.A, R2.Pin_0
  N20: LED1.cathode, R1.Pin_1
  N21: LED2.cathode, R3.Pin_1

custom parts:
  RFID-RC522-v2: A simple China made RFID-RC522 Reader; do check the pin labels, as this is a MFRC522 based clone.
